# Fritzing sketch HM10_Arduino_Schematic (saved by Fritzing 0.9.3b)
breadboards: 1

parts:
  Part1 = Arduino Uno (Rev3)
  Part2 = Bluetooth HM-10

nets:
  N1: Part1.D10_PWM/SS, Part2.RXD
  N2: Part1.D11_PWM/MOSI, Part2.TXD
  3V3: Part1.3V3, Part2.VCC
  GND: Part1.GND, Part2.GND

// code stored in the sketch: BabySafe_BLE_HM-10.ino
#include <SoftwareSerial.h>

SoftwareSerial BTSerial(11,10); // RX, TX  

void setup(){
  Serial.begin(9600);
  Serial.println("AT commands: ");
  BTSerial.begin(9600); //baud rate
  //while(!Serial);
  
  }

  void loop () {
    //read from the HM-10 and print in the Serial
    if(BTSerial.available())
      Serial.write(BTSerial.read());

    //read from the Serial and print to the HM-10
    if(Serial.available())
      BTSerial.write(Serial.read());
  }
